// Digital circuit SR Latch.dig as structural Verilog
module SR_Latch (
  input  Set,
  input  Reset,
  input  R,
  input  S,
  output Qa_bit,
  output Qa,
  output Qb
);

  wire _7402_1_pin8;

  _7402 _7402_1 (
    .pin2(1'b0), .pin3(1'b0), .pin5(1'b0), .pin6(1'b0), .pin7(1'b0), .pin8(_7402_1_pin8), .pin9(Reset),
    .pin10(Qa_bit), .pin11(Set), .pin12(Qa_bit), .pin13(_7402_1_pin8), .pin14(1'b1));  // open: pin1, pin4
  nor nor_1 (Qa, R, Qb);
  nor nor_2 (Qb, Qa, S);
endmodule
