// Digital circuit Gated D Latch.dig as structural Verilog
module Gated_D_Latch (
  input  Clock,
  input  D_set,
  input  D,
  input  Clk,
  output Qa_bit,
  output Q,
  output Q_not
);

  wire _7400_1_pin3, _7400_1_pin6, _7400_1_pin8, nand_1_out, nand_2_out, not_1_out, not_2_out;

  not not_1 (not_1_out, D_set);
  _7400 _7400_1 (
    .pin1(D_set), .pin2(Clock), .pin3(_7400_1_pin3), .pin4(not_1_out), .pin5(Clock), .pin6(_7400_1_pin6),
    .pin7(1'b0), .pin8(_7400_1_pin8), .pin9(Qa_bit), .pin10(_7400_1_pin6), .pin11(Qa_bit),
    .pin12(_7400_1_pin8), .pin13(_7400_1_pin3), .pin14(1'b1));
  not not_2 (not_2_out, D);
  nand nand_1 (nand_1_out, D, Clk);
  nand nand_2 (nand_2_out, Clk, not_2_out);
  nand nand_3 (Q, nand_1_out, Q_not);
  nand nand_4 (Q_not, Q, nand_2_out);
endmodule
