// Digital circuit Master Slave D Flip Flop.dig as structural Verilog
module Master_Slave_D_Flip_Flop (
  input  D_set,
  input  Clock,
  input  D,
  input  Clk,
  output Q_slave,
  output Q_master,
  output Qm_not,
  output Qm,
  output Qs_not,
  output Qs
);

  wire _7400_1_pin3, _7400_1_pin6, _7400_1_pin8, _7400_2_pin3, _7400_2_pin6, _7400_2_pin8, _7404_1_pin6,
       _7404_2_pin8, _7404_2_pin12, nand_1_out, nand_2_out, nand_5_out, nand_6_out, not_1_out, not_2_out,
       not_3_out;

  _7404 _7404_1 (
    .pin1(1'b0), .pin3(1'b0), .pin5(D_set), .pin6(_7404_1_pin6), .pin7(1'b0), .pin9(1'b0), .pin11(1'b0),
    .pin13(1'b0), .pin14(1'b1));  // open: pin2, pin4, pin8, pin10, pin12
  not not_1 (not_1_out, D);
  nand nand_1 (nand_1_out, D, Clk);
  nand nand_2 (nand_2_out, not_1_out, Clk);
  nand nand_3 (Qm, nand_1_out, Qm_not);
  nand nand_4 (Qm_not, Qm, nand_2_out);
  _7400 _7400_1 (
    .pin1(D_set), .pin2(Clock), .pin3(_7400_1_pin3), .pin4(_7404_1_pin6), .pin5(Clock), .pin6(_7400_1_pin6),
    .pin7(1'b0), .pin8(_7400_1_pin8), .pin9(_7400_1_pin6), .pin10(Q_master), .pin11(Q_master),
    .pin12(_7400_1_pin8), .pin13(_7400_1_pin3), .pin14(1'b1));
  not not_2 (not_2_out, Clk);
  not not_3 (not_3_out, Qm);
  _7404 _7404_2 (
    .pin1(1'b0), .pin3(1'b0), .pin5(1'b0), .pin7(1'b0), .pin8(_7404_2_pin8), .pin9(Clock), .pin11(1'b0),
    .pin12(_7404_2_pin12), .pin13(Q_master), .pin14(1'b1));  // open: pin2, pin4, pin6, pin10
  nand nand_5 (nand_5_out, Qm, not_2_out);
  nand nand_6 (nand_6_out, not_3_out, not_2_out);
  nand nand_7 (Qs, nand_5_out, Qs_not);
  nand nand_8 (Qs_not, Qs, nand_6_out);
  _7400 _7400_2 (
    .pin1(Q_master), .pin2(_7404_2_pin8), .pin3(_7400_2_pin3), .pin4(_7404_2_pin12), .pin5(_7404_2_pin8),
    .pin6(_7400_2_pin6), .pin7(1'b0), .pin8(_7400_2_pin8), .pin9(_7400_2_pin6), .pin10(Q_slave),
    .pin11(Q_slave), .pin12(_7400_2_pin8), .pin13(_7400_2_pin3), .pin14(1'b1));
endmodule
