// Digital circuit 4 Bit D Type Register.dig as structural Verilog
module _4_Bit_D_Type_Register (
  input  Clear,
  input  D0,
  input  D1,
  input  D2,
  input  D3,
  input  Clock,
  output Q0,
  output Q1,
  output Q2,
  output Q3
);

  _74173 _74173_1 (
    .pin1(1'b0), .pin2(1'b0), .pin3(Q0), .pin4(Q1), .pin5(Q2), .pin6(Q3), .pin7(Clock), .pin8(1'b0),
    .pin9(1'b0), .pin10(1'b0), .pin11(D3), .pin12(D2), .pin13(D1), .pin14(D0), .pin15(Clear), .pin16(1'b1));

  // Notes on the sheet:
  //   Data In
  //   Stored Memory
endmodule
