// Digital circuit 4 Bit Binary Adder Module.dig as structural Verilog
module _4_Bit_Binary_Adder_Module (
  input  Count_1,
  input  Count_2,
  input  Clear,
  output A0,
  output A1,
  output A2,
  output A3,
  output B0,
  output B1,
  output B2,
  output B3,
  output S0,
  output S1,
  output S2,
  output S3,
  output S4
);

  _74161 Counter (
    .pin1(Clear), .pin2(Count_1), .pin3(1'b0), .pin4(1'b0), .pin5(1'b0), .pin6(1'b0), .pin7(1'b1),
    .pin8(1'b0), .pin9(1'b1), .pin10(1'b1), .pin11(A3), .pin12(A2), .pin13(A1), .pin14(A0), .pin16(1'b1));  // open: pin15
  _74161 Counter_2 (
    .pin1(Clear), .pin2(Count_2), .pin3(1'b0), .pin4(1'b0), .pin5(1'b0), .pin6(1'b0), .pin7(1'b1),
    .pin8(1'b0), .pin9(1'b1), .pin10(1'b1), .pin11(B3), .pin12(B2), .pin13(B1), .pin14(B0), .pin16(1'b1));  // open: pin15
  _74283 _74283_1 (
    .pin1(S1), .pin2(B1), .pin3(A1), .pin4(S0), .pin5(A0), .pin6(B0), .pin7(1'b0), .pin8(1'b0), .pin9(S4),
    .pin10(S3), .pin11(B3), .pin12(A3), .pin13(S2), .pin14(A2), .pin15(B2), .pin16(1'b1));

  // Notes on the sheet:
  //   Addend #1
  //   Addend #2
  //   Sum
endmodule
