// Digital circuit 7 segment HEX decoder.dig as structural Verilog
module _7_segment_HEX_decoder (
  input  A,
  input  B,
  input  C,
  input  D
);

  wire and_1_out, and_2_out, and_3_out, and_4_out, and_5_out, and_6_out, and_7_out, and_8_out, and_9_out,
       and_10_out, and_11_out, and_12_out, and_13_out, and_14_out, and_15_out, and_16_out, and_17_out,
       and_18_out, and_19_out, and_20_out, and_21_out, and_22_out, and_23_out, not_1_out, not_2_out,
       not_3_out, not_4_out, or_1_out, or_2_out, or_3_out, or_4_out, or_5_out, or_6_out, or_7_out, or_8_out,
       or_9_out, or_10_out, or_11_out, or_12_out, or_13_out, or_14_out, or_15_out, or_16_out, or_17_out,
       or_18_out, or_19_out, or_20_out, or_21_out, or_22_out;

  not not_1 (not_1_out, A);
  not not_2 (not_2_out, B);
  not not_3 (not_3_out, C);
  not not_4 (not_4_out, D);
  and and_1 (and_1_out, A, B);
  and and_2 (and_2_out, not_1_out, B);
  and and_3 (and_3_out, A, not_2_out);
  and and_4 (and_4_out, not_1_out, not_2_out);
  and and_5 (and_5_out, C, D);
  and and_6 (and_6_out, not_3_out, D);
  and and_7 (and_7_out, C, not_4_out);
  and and_8 (and_8_out, not_3_out, not_4_out);
  and and_9 (and_9_out, and_3_out, and_8_out);
  and and_10 (and_10_out, and_1_out, and_7_out);
  and and_11 (and_11_out, and_4_out, and_7_out);
  and and_12 (and_12_out, and_4_out, and_5_out);
  and and_13 (and_13_out, and_1_out, and_5_out);
  and and_14 (and_14_out, and_2_out, and_5_out);
  and and_15 (and_15_out, and_3_out, and_7_out);
  and and_16 (and_16_out, and_3_out, and_5_out);
  and and_17 (and_17_out, and_2_out, and_8_out);
  and and_18 (and_18_out, and_1_out, and_6_out);
  and and_19 (and_19_out, and_1_out, and_8_out);
  and and_20 (and_20_out, and_2_out, and_7_out);
  and and_21 (and_21_out, and_2_out, and_6_out);
  and and_22 (and_22_out, and_3_out, and_6_out);
  and and_23 (and_23_out, and_4_out, and_8_out);
  or or_1 (or_1_out, and_9_out, and_11_out);
  or or_2 (or_2_out, and_12_out, and_13_out);
  or or_3 (or_3_out, and_9_out, and_10_out);
  or or_4 (or_4_out, or_2_out, and_14_out);
  or or_5 (or_5_out, or_1_out, and_16_out);
  or or_6 (or_6_out, or_4_out, and_15_out);
  or or_7 (or_7_out, and_20_out, and_18_out);
  or or_8 (or_8_out, or_4_out, and_17_out);
  or or_9 (or_9_out, or_1_out, and_10_out);
  or or_10 (or_10_out, and_13_out, and_21_out);
  or or_11 (or_11_out, or_1_out, and_15_out);
  or or_12 (or_12_out, and_22_out, and_19_out);
  or or_13 (or_13_out, or_3_out, and_16_out);
  or or_14 (or_14_out, and_19_out, and_17_out);
  or or_15 (or_15_out, or_3_out, and_23_out);
  or or_16 (or_16_out, or_5_out, and_18_out);
  or or_17 (or_17_out, or_6_out, or_7_out);
  or or_18 (or_18_out, or_9_out, or_10_out);
  or or_19 (or_19_out, or_11_out, or_12_out);
  or or_20 (or_20_out, or_13_out, or_14_out);
  or or_21 (or_21_out, or_15_out, and_12_out);
  or or_22 (or_22_out, or_19_out, and_10_out);
  Seven_Seg #(.commonConnectionType("anode"), .commonCathode("true")) seven_seg_1 (
    .a(or_16_out), .b(or_17_out), .c(or_8_out), .d(or_18_out), .e(or_22_out), .f(or_20_out), .g(or_21_out),
    .dp(1'b0), .common(1'b1));

  // Notes on the sheet:
  //   A B
  //   !A B
  //   A !B
  //   !A !B
  //   C D
  //   !C D
  //   C !D
  //   !C !D
  //   A !B !C !D
  //   A B C !D
  //   !A !B C !D
  //   !A !B C D
  //   A B C D
  //   !A B C D
  //   A !B C !D
  //   A !B C D
  //   !A B !C !D
  //   A B !C D
  //   A B !C !D
  //   !A B C !D
  //   !A B !C D
  //   A !B !C D
  //   !A !B !C !D
  //   a
  //   b
  //   c
  //   d
  //   e
  //   f
  //   g
endmodule
