// Digital circuit 7_seg_decoder_7447_CA.dig as structural Verilog
module _7_seg_decoder_7447_CA (
  input  b3,
  input  b2,
  input  b1,
  input  b0,
  output a,
  output b,
  output c,
  output d,
  output e,
  output f,
  output g
);

  _7447 _7447_1 (
    .pin1(b1), .pin2(b2), .pin3(1'b1), .pin4(1'b1), .pin5(1'b1), .pin6(b3), .pin7(b0), .pin8(1'b0), .pin9(e),
    .pin10(d), .pin11(c), .pin12(b), .pin13(a), .pin14(g), .pin15(f), .pin16(1'b1));
endmodule
